// Logisim project Full adder.circ as structural Verilog: 1 circuit, main circuit main
module main (
  input  A,
  input  B,
  input  Carry,
  output Sum,
  output Carry_out
);

  wire and_1_out, and_2_out, xor_1_out;

  xor xor_1 (xor_1_out, A, B);
  xor xor_2 (Sum, xor_1_out, Carry);
  and and_1 (and_1_out, B, A);
  and and_2 (and_2_out, xor_1_out, Carry);
  or or_1 (Carry_out, and_1_out, and_2_out);
endmodule
